// Logisim project func_schematic.circ as structural Verilog: 1 circuit, main circuit main
module main (
);

  wire and_1_out, and_2_out, and_3_out, and_4_out, and_5_out, and_6_out, and_7_out, and_8_out, and_9_out,
       and_10_out, controlled_buffer_1_out, controlled_buffer_2_out, controlled_buffer_3_out,
       controlled_buffer_4_out, controlled_buffer_6_out, controlled_buffer_8_out, nand_1_out, nand_2_out,
       nand_3_out, nand_4_out, nand_5_out, nand_6_out, nand_7_out, nand_8_out, nand_9_out, nand_10_out,
       nand_11_out, nand_12_out, nand_13_out, nand_14_out, nand_15_out, nand_16_out, not_1_out, not_2_out,
       not_3_out, not_4_out, not_5_out, not_6_out, not_7_out, not_8_out, not_9_out, not_10_out, not_11_out,
       not_12_out, not_13_out, not_14_out, not_15_out, not_16_out, not_17_out, not_18_out, not_19_out,
       not_20_out, not_21_out, not_22_out, not_23_out, not_24_out, not_25_out, undriven, undriven_2,
       undriven_3;

  not not_1 (not_1_out, undriven_2);
  and and_1 (and_1_out, not_1_out, undriven_3);
  and and_2 (and_2_out, undriven_3, undriven_2);
  not not_2 (not_2_out, undriven);
  not not_3 (not_3_out, undriven);
  and and_3 (and_3_out, undriven, and_1_out);
  and and_4 (and_4_out, and_1_out, not_2_out);
  and and_5 (and_5_out, undriven, and_1_out);
  and and_6 (and_6_out, and_1_out, not_3_out);
  not not_4 (not_4_out, controlled_buffer_2_out);
  not not_5 (not_5_out, controlled_buffer_4_out);
  nand nand_1 (nand_1_out, controlled_buffer_2_out, and_3_out);
  nand nand_2 (nand_2_out, and_3_out, not_4_out);
  nand nand_3 (nand_3_out, controlled_buffer_4_out, and_5_out);
  nand nand_4 (nand_4_out, and_5_out, not_5_out);
  nand nand_5 (nand_5_out, nand_1_out, nand_6_out);
  nand nand_6 (nand_6_out, nand_5_out, nand_2_out);
  nand nand_7 (nand_7_out, nand_3_out, nand_8_out);
  nand nand_8 (nand_8_out, nand_7_out, nand_4_out);
  assign controlled_buffer_1_out = not_6_out ? nand_5_out : 1'bz;  // Controlled_Buffer controlled_buffer_1
  not not_6 (not_6_out, not_7_out);
  not not_7 (not_7_out, and_4_out);
  assign controlled_buffer_2_out = not_8_out ? controlled_buffer_1_out : 1'bz;  // Controlled_Buffer controlled_buffer_2
  not not_8 (not_8_out, not_9_out);
  not not_9 (not_9_out, and_3_out);
  assign controlled_buffer_3_out = not_10_out ? nand_7_out : 1'bz;  // Controlled_Buffer controlled_buffer_3
  not not_10 (not_10_out, not_11_out);
  not not_11 (not_11_out, and_6_out);
  assign controlled_buffer_4_out = not_12_out ? controlled_buffer_3_out : 1'bz;  // Controlled_Buffer controlled_buffer_4
  not not_12 (not_12_out, not_13_out);
  not not_13 (not_13_out, and_5_out);
  and and_7 (and_7_out, undriven, and_2_out);
  and and_8 (and_8_out, and_2_out, not_14_out);
  not not_14 (not_14_out, undriven);
  and and_9 (and_9_out, undriven, and_2_out);
  and and_10 (and_10_out, and_2_out, not_15_out);
  not not_15 (not_15_out, undriven);
  not not_16 (not_16_out, controlled_buffer_6_out);
  not not_17 (not_17_out, controlled_buffer_8_out);
  nand nand_9 (nand_9_out, controlled_buffer_6_out, and_7_out);
  nand nand_10 (nand_10_out, and_7_out, not_16_out);
  nand nand_11 (nand_11_out, controlled_buffer_8_out, and_9_out);
  nand nand_12 (nand_12_out, and_9_out, not_17_out);
  nand nand_13 (nand_13_out, nand_9_out, nand_14_out);
  nand nand_14 (nand_14_out, nand_13_out, nand_10_out);
  nand nand_15 (nand_15_out, nand_11_out, nand_16_out);
  nand nand_16 (nand_16_out, nand_15_out, nand_12_out);
  assign controlled_buffer_1_out = not_18_out ? nand_13_out : 1'bz;  // Controlled_Buffer controlled_buffer_5
  not not_18 (not_18_out, not_19_out);
  not not_19 (not_19_out, and_8_out);
  assign controlled_buffer_6_out = not_20_out ? controlled_buffer_1_out : 1'bz;  // Controlled_Buffer controlled_buffer_6
  not not_20 (not_20_out, not_21_out);
  not not_21 (not_21_out, and_7_out);
  assign controlled_buffer_3_out = not_22_out ? nand_15_out : 1'bz;  // Controlled_Buffer controlled_buffer_7
  not not_22 (not_22_out, not_23_out);
  not not_23 (not_23_out, and_10_out);
  assign controlled_buffer_8_out = not_24_out ? controlled_buffer_3_out : 1'bz;  // Controlled_Buffer controlled_buffer_8
  not not_24 (not_24_out, not_25_out);
  not not_25 (not_25_out, and_9_out);

  // Notes on the sheet:
  //   Enable
  //   Read/Write
  //   Address0
  //   NOT4-1
  //   NOT4-3
  //   AND1-1
  //   AND1-2
  //   AND1-3
  //   AND1-4
  //   NOT1-1
  //   NOT1-2
  //   NAND1-1
  //   NAND1-2
  //   NAND2-1
  //   NAND2-2
  //   NAND1-3
  //   NAND1-4
  //   NOT2-5
  //   NAND2-3
  //   NAND2-4
  //   NOT3-1
  //   BUF1-1
  //   NOT2-1
  //   BUF1-3
  //   BUF1-2
  //   NOT2-3
  //   BUF1-4
  //   NOT4-2
  //   NOT4-4
  //   AND2-1
  //   AND2-2
  //   AND2-3
  //   AND2-4
  //   NOT1-3
  //   NOT1-4
  //   NAND3-1
  //   NAND3-2
  //   NAND4-1
  //   NAND4-2
  //   NAND3-3
  //   NAND3-4
  //   NOT2-6
  //   NAND4-3
  //   NAND4-4
  //   NOT2-2
  //   BUF2-1
  //   BUF2-3
  //   BUF2-2
  //   BUF2-4
  //   NOT2-2
  //   NOT2-4
  //   NANDx-x: 7400
  //   NOTx-x: 7404
  //   BUFx-x: 74125
  //   ANDx-x: 7408
  //   Data0
  //   Data1
endmodule
